// Logisim project MEM.circ as structural Verilog
module block1 (
  input  in_1,
  input  in_2,
  input  in_3,
  input  in_4,
  input  E,
  output F1,
  output F2,
  output F3,
  output F4,
  output F5
);

  wire and_1_out, and_2_out, and_3_out, and_4_out, and_5_out, and_6_out, and_7_out, and_8_out, and_9_out,
       and_10_out, and_11_out, and_12_out, and_13_out, and_14_out, and_15_out, and_16_out, and_17_out,
       and_18_out, and_19_out, and_20_out, and_21_out, and_22_out, and_23_out, and_24_out, and_25_out,
       and_26_out, and_27_out, not_1_out, not_2_out, not_3_out, not_4_out, not_5_out;

  not not_1 (not_1_out, in_1);
  not not_2 (not_2_out, in_2);
  not not_3 (not_3_out, in_3);
  not not_4 (not_4_out, in_4);
  not not_5 (not_5_out, E);
  and and_1 (and_1_out, not_5_out, not_4_out, in_3, not_1_out);
  and and_2 (and_2_out, E, not_3_out, not_2_out, not_1_out);
  and and_3 (and_3_out, E, in_4, not_1_out);
  and and_4 (and_4_out, in_4, not_3_out, not_1_out);
  and and_5 (and_5_out, in_4, not_2_out, not_1_out);
  and and_6 (and_6_out, E, in_4, not_3_out, in_2);
  and and_7 (and_7_out, not_4_out, not_3_out, not_2_out, in_1);
  and and_8 (and_8_out, not_5_out, not_3_out, not_2_out, not_1_out);
  and and_9 (and_9_out, E, not_4_out, in_3);
  and and_10 (and_10_out, not_5_out, not_4_out, not_3_out);
  and and_11 (and_11_out, not_5_out, not_4_out, not_2_out, in_1);
  and and_12 (and_12_out, not_5_out, not_3_out, not_1_out, in_2);
  and and_13 (and_13_out, E, in_4, not_2_out, not_1_out);
  and and_14 (and_14_out, not_3_out, in_1, not_2_out);
  and and_15 (and_15_out, not_4_out, not_3_out, not_1_out);
  and and_16 (and_16_out, E, not_3_out, not_2_out, not_1_out);
  and and_17 (and_17_out, not_4_out, in_3, in_1);
  and and_18 (and_18_out, not_5_out, in_3, not_2_out);
  and and_19 (and_19_out, not_5_out, not_2_out, not_4_out);
  and and_20 (and_20_out, in_2, in_1);
  and and_21 (and_21_out, not_5_out, in_1);
  and and_22 (and_22_out, E, not_4_out, not_2_out, not_1_out);
  and and_23 (and_23_out, not_4_out, not_3_out, in_2, not_1_out);
  and and_24 (and_24_out, not_5_out, in_4, not_3_out, not_1_out);
  and and_25 (and_25_out, in_4, in_3, in_1);
  and and_26 (and_26_out, not_5_out, not_4_out, in_1);
  and and_27 (and_27_out, not_5_out, in_3, not_4_out);
  or or_1 (F1, and_1_out, and_2_out, and_3_out, and_4_out, and_5_out);
  or or_2 (F2, and_6_out, and_7_out, and_8_out, and_9_out, and_10_out);
  or or_3 (F3, and_11_out, and_12_out, and_13_out, and_14_out, and_15_out);
  or or_4 (F4, and_16_out, and_17_out, and_18_out, and_19_out, and_20_out, and_21_out);
  or or_5 (F5, and_22_out, and_23_out, and_24_out, and_25_out, and_26_out, and_27_out);

  // Notes on the sheet:
  //   A
  //   A
  //   A
  //   A
  //   A
  //   MSB
  //   B
  //   B
  //   B
  //   B
  //   B
  //   C
  //   C
  //   C
  //   C
  //   C
  //   D
  //   D
  //   D
  //   E
  //   D
  //   E
  //   D
  //   E
  //   E
  //   LSB
  //   MSB
  //   LSB
endmodule

module block3 (
  input  A,
  input  B,
  input  C,
  input  D,
  input  E,
  output out_6,
  output O4,
  output O3,
  output O2,
  output O1
);

  wire and_1_out, and_2_out, and_3_out, and_4_out, and_5_out, and_6_out, and_7_out, and_8_out, and_9_out,
       and_10_out, and_11_out, and_12_out, and_13_out, and_14_out, and_15_out, and_16_out, and_17_out,
       and_18_out, and_19_out, and_20_out, and_21_out, and_22_out, and_23_out, and_24_out, and_25_out,
       and_26_out, and_27_out, and_28_out, not_1_out, not_2_out, not_3_out, not_4_out, not_5_out;

  not not_1 (not_1_out, A);
  not not_2 (not_2_out, B);
  not not_3 (not_3_out, C);
  not not_4 (not_4_out, D);
  not not_5 (not_5_out, E);
  and and_1 (and_1_out, E, D, C, A);
  and and_2 (and_2_out, not_5_out, D, not_3_out, A);
  and and_3 (and_3_out, not_5_out, not_3_out, B, not_1_out);
  and and_4 (and_4_out, E, not_4_out, not_2_out, not_1_out);
  and and_5 (and_5_out, not_4_out, not_3_out, not_2_out, not_1_out);
  and and_6 (and_6_out, E, C, B);
  and and_7 (and_7_out, not_4_out, C, B);
  and and_8 (and_8_out, E, D, not_3_out, not_2_out, not_1_out);
  and and_9 (and_9_out, not_5_out, not_4_out, A);
  and and_10 (and_10_out, not_5_out, not_4_out, B);
  and and_11 (and_11_out, not_5_out, C, not_2_out);
  and and_12 (and_12_out, B, A);
  and and_13 (and_13_out, E, not_4_out, not_3_out, not_1_out);
  and and_14 (and_14_out, D, not_3_out, A);
  and and_15 (and_15_out, not_5_out, C, A);
  and and_16 (and_16_out, D, C, B);
  and and_17 (and_17_out, E, not_4_out, B);
  and and_18 (and_18_out, not_5_out, D, not_2_out);
  and and_19 (and_19_out, not_5_out, not_3_out, not_2_out, A);
  and and_20 (and_20_out, E, C, not_2_out, not_1_out);
  and and_21 (and_21_out, E, D, not_1_out);
  and and_22 (and_22_out, D, not_2_out, not_1_out);
  and and_23 (and_23_out, D, C);
  and and_24 (and_24_out, not_5_out, D, A);
  and and_25 (and_25_out, not_5_out, not_4_out, C);
  and and_26 (and_26_out, E, D, not_3_out);
  and and_27 (and_27_out, not_4_out, C, not_2_out);
  and and_28 (and_28_out, not_3_out, not_2_out, not_1_out);
  or or_1 (out_6, and_1_out, and_2_out, and_3_out, and_4_out, and_5_out, and_6_out, and_7_out);
  or or_2 (O4, and_8_out, and_9_out, and_10_out, and_11_out, and_12_out);
  or or_3 (O3, and_13_out, and_14_out, and_15_out, and_16_out, and_17_out, and_18_out);
  or or_4 (O2, and_19_out, and_20_out, and_21_out, and_22_out, and_23_out);
  or or_5 (O1, and_24_out, and_25_out, and_26_out, and_27_out, and_28_out);
endmodule

module block4 (
  input  in_1,
  input  in_2,
  input  in_3,
  input  D,
  input  in_5,
  output _05,
  output out_7,
  output out_8,
  output O2,
  output O1
);

  wire and_1_out, and_2_out, and_3_out, and_4_out, and_5_out, and_6_out, and_7_out, and_8_out, and_9_out,
       and_10_out, and_11_out, and_12_out, and_13_out, and_14_out, and_15_out, and_16_out, and_17_out,
       and_18_out, and_19_out, and_20_out, and_21_out, and_22_out, and_23_out, and_24_out, and_25_out,
       and_26_out, and_27_out, and_28_out, and_29_out, and_30_out, and_31_out, and_32_out, not_1_out,
       not_2_out, not_3_out, not_4_out, not_5_out;

  not not_1 (not_1_out, in_1);
  not not_2 (not_2_out, in_2);
  not not_3 (not_3_out, in_3);
  not not_4 (not_4_out, D);
  not not_5 (not_5_out, in_5);
  and and_1 (and_1_out, not_5_out, D, in_3, in_1);
  and and_2 (and_2_out, not_5_out, not_3_out, in_2, not_1_out);
  and and_3 (and_3_out, in_5, not_3_out, not_2_out, not_1_out);
  and and_4 (and_4_out, in_5, in_2, in_1);
  and and_5 (and_5_out, in_5, D, not_1_out);
  and and_6 (and_6_out, D, in_2);
  and and_7 (and_7_out, in_5, not_4_out, not_3_out, not_2_out, not_1_out);
  and and_8 (and_8_out, not_5_out, not_4_out, not_2_out, in_1);
  and and_9 (and_9_out, not_5_out, D, not_2_out, not_1_out);
  and and_10 (and_10_out, in_5, D, in_1);
  and and_11 (and_11_out, not_5_out, in_3, not_2_out);
  and and_12 (and_12_out, in_3, in_1);
  and and_13 (and_13_out, in_5, D, in_3, in_1);
  and and_14 (and_14_out, not_5_out, not_4_out, in_3, in_1);
  and and_15 (and_15_out, in_5, not_4_out, not_3_out, in_1);
  and and_16 (and_16_out, not_5_out, D, not_2_out, not_1_out);
  and and_17 (and_17_out, not_5_out, not_4_out, not_3_out, not_1_out);
  and and_18 (and_18_out, D, in_3, in_2);
  and and_19 (and_19_out, in_5, not_4_out, in_2);
  and and_20 (and_20_out, not_5_out, not_4_out, not_2_out, in_1);
  and and_21 (and_21_out, in_5, D, not_3_out, not_2_out);
  and and_22 (and_22_out, in_5, D, in_1);
  and and_23 (and_23_out, in_5, not_3_out, in_1);
  and and_24 (and_24_out, not_4_out, in_3, in_2);
  and and_25 (and_25_out, not_5_out, D, in_2);
  and and_26 (and_26_out, not_3_out, not_2_out, in_1);
  and and_27 (and_27_out, not_4_out, not_3_out, not_2_out, in_1);
  and and_28 (and_28_out, D, in_3, not_2_out, not_1_out);
  and and_29 (and_29_out, not_5_out, not_3_out, in_2);
  and and_30 (and_30_out, not_5_out, D, in_3);
  and and_31 (and_31_out, not_5_out, not_4_out, not_2_out);
  and and_32 (and_32_out, not_5_out, in_1);
  or or_1 (_05, and_1_out, and_2_out, and_3_out, and_4_out, and_5_out, and_6_out);
  or or_2 (out_7, and_7_out, and_8_out, and_9_out, and_10_out, and_11_out, and_12_out);
  or or_3 (out_8, and_13_out, and_14_out, and_15_out, and_16_out, and_17_out, and_18_out, and_19_out);
  or or_4 (O2, and_20_out, and_21_out, and_22_out, and_23_out, and_24_out, and_25_out, and_26_out);
  or or_5 (O1, and_27_out, and_28_out, and_29_out, and_30_out, and_31_out, and_32_out);

  // Notes on the sheet:
  //   A
  //   B
  //   C
  //   E
  //   O4
  //   O3
endmodule

module Decoder (
  input  in_1,
  input  in_2,
  input  in_3,
  input  in_4,
  input  in_5,
  output z,
  output y,
  output x,
  output w,
  output v,
  output u,
  output t,
  output s,
  output r,
  output q,
  output p,
  output o,
  output n,
  output m,
  output l,
  output k,
  output j,
  output i,
  output h,
  output g,
  output f,
  output e,
  output d,
  output c,
  output b,
  output a
);

  wire not_1_out, not_2_out, not_3_out, not_4_out, not_5_out;

  not not_1 (not_1_out, in_1);
  not not_2 (not_2_out, in_2);
  not not_3 (not_3_out, in_3);
  not not_4 (not_4_out, in_4);
  not not_5 (not_5_out, in_5);
  and and_1 (z, in_5, not_4_out, not_3_out, in_2, in_1);
  and and_2 (y, not_5_out, not_4_out, not_3_out, in_2, in_1);
  and and_3 (x, in_5, in_4, in_3, not_2_out, in_1);
  and and_4 (w, not_5_out, in_4, in_3, not_2_out, in_1);
  and and_5 (v, in_5, not_4_out, in_3, not_2_out, in_1);
  and and_6 (u, not_5_out, not_4_out, in_3, not_2_out, in_1);
  and and_7 (t, in_5, in_4, not_3_out, not_2_out, in_1);
  and and_8 (s, not_5_out, in_4, not_3_out, not_2_out, in_1);
  and and_9 (r, in_5, not_4_out, not_3_out, not_2_out, in_1);
  and and_10 (q, not_5_out, not_4_out, not_3_out, not_2_out, in_1);
  and and_11 (p, in_5, in_4, in_3, in_2, not_1_out);
  and and_12 (o, not_5_out, in_4, in_3, in_2, not_1_out);
  and and_13 (n, in_5, not_4_out, in_3, in_2, not_1_out);
  and and_14 (m, not_5_out, not_4_out, in_3, in_2, not_1_out);
  and and_15 (l, in_5, in_4, not_3_out, in_2, not_1_out);
  and and_16 (k, not_5_out, in_4, not_3_out, in_2, not_1_out);
  and and_17 (j, in_5, not_4_out, not_3_out, in_2, not_1_out);
  and and_18 (i, not_5_out, not_4_out, not_3_out, in_2, not_1_out);
  and and_19 (h, in_5, in_4, in_3, not_2_out, not_1_out);
  and and_20 (g, not_5_out, in_4, in_3, not_2_out, not_1_out);
  and and_21 (f, in_5, not_4_out, in_3, not_2_out, not_1_out);
  and and_22 (e, not_5_out, not_4_out, in_3, not_2_out, not_1_out);
  and and_23 (d, in_5, in_4, not_3_out, not_2_out, not_1_out);
  and and_24 (c, not_5_out, in_4, not_3_out, not_2_out, not_1_out);
  and and_25 (b, in_5, not_4_out, not_3_out, not_2_out, not_1_out);
  and and_26 (a, not_5_out, not_4_out, not_3_out, not_2_out, not_1_out);

  // Notes on the sheet:
  //   MSB
  //   LSB
endmodule

module block2 (
  input  in_1,
  input  B,
  input  C,
  input  D,
  input  E,
  output F1,
  output F2,
  output F3,
  output F4,
  output F5
);

  wire and_1_out, and_2_out, and_3_out, and_4_out, and_5_out, and_6_out, and_7_out, and_8_out, and_9_out,
       and_10_out, and_11_out, and_12_out, and_13_out, and_14_out, and_15_out, and_16_out, and_17_out,
       and_18_out, and_19_out, and_20_out, and_21_out, and_22_out, and_23_out, and_24_out, and_25_out,
       and_26_out, and_27_out, and_28_out, not_1_out, not_2_out, not_3_out, not_4_out, not_5_out;

  not not_1 (not_1_out, in_1);
  not not_2 (not_2_out, B);
  not not_3 (not_3_out, C);
  not not_4 (not_4_out, D);
  not not_5 (not_5_out, E);
  and and_1 (and_1_out, not_1_out, B, not_4_out, E);
  and and_2 (and_2_out, not_1_out, not_2_out, not_3_out, D);
  and and_3 (and_3_out, E, not_3_out, B);
  and and_4 (and_4_out, not_5_out, not_4_out, C);
  and and_5 (and_5_out, not_3_out, B, not_1_out);
  and and_6 (and_6_out, not_4_out, not_3_out, not_1_out);
  and and_7 (and_7_out, E, not_3_out, not_2_out, in_1);
  and and_8 (and_8_out, not_5_out, not_4_out, not_3_out, B);
  and and_9 (and_9_out, not_5_out, D, C, not_2_out);
  and and_10 (and_10_out, not_5_out, not_4_out, in_1);
  and and_11 (and_11_out, E, C, B);
  and and_12 (and_12_out, not_1_out, C, D);
  and and_13 (and_13_out, not_5_out, D, not_3_out, in_1);
  and and_14 (and_14_out, E, not_4_out, in_1, not_3_out);
  and and_15 (and_15_out, not_4_out, not_3_out, not_2_out, not_1_out);
  and and_16 (and_16_out, D, not_5_out, B);
  and and_17 (and_17_out, E, C, not_1_out);
  and and_18 (and_18_out, not_1_out, not_2_out, C, not_4_out);
  and and_19 (and_19_out, not_2_out, not_3_out, not_5_out, not_4_out);
  and and_20 (and_20_out, not_5_out, C, D);
  and and_21 (and_21_out, not_5_out, D, not_1_out);
  and and_22 (and_22_out, E, D, not_3_out, in_1);
  and and_23 (and_23_out, not_5_out, not_4_out, not_3_out, not_2_out);
  and and_24 (and_24_out, not_5_out, not_3_out, not_2_out, not_1_out);
  and and_25 (and_25_out, not_4_out, C, B);
  and and_26 (and_26_out, E, C, not_1_out);
  and and_27 (and_27_out, E, not_1_out, not_4_out);
  and and_28 (and_28_out, not_4_out, C, in_1);
  or or_1 (F2, and_7_out, and_8_out, and_9_out, and_10_out, and_11_out);
  or or_2 (F3, and_12_out, and_13_out, and_14_out, and_15_out, and_16_out, and_17_out);
  or or_3 (F4, and_1_out, and_18_out, and_2_out, and_19_out, and_20_out, and_21_out);
  or or_4 (F5, and_22_out, and_23_out, and_24_out, and_25_out, and_26_out, and_27_out, and_28_out);
  or or_5 (F1, and_3_out, and_4_out, and_5_out, and_6_out);

  // Notes on the sheet:
  //   A
  //   A
  //   A
  //   A
  //   A
  //   MSB
  //   B
  //   B
  //   B
  //   B
  //   C
  //   C
  //   C
  //   C
  //   D
  //   D
  //   D
  //   E
  //   D
  //   E
  //   E
  //   E
  //   LSB
  //   MSB
  //   LSB
endmodule

module Encoder (
  input  _1,
  input  _2,
  input  _3,
  input  _4,
  input  _5,
  input  _6,
  input  _7,
  input  _8,
  input  _9,
  input  _10,
  input  _11,
  input  _12,
  input  _13,
  input  _14,
  input  _15,
  input  _16,
  input  _17,
  input  _18,
  input  _19,
  input  _20,
  input  _21,
  input  _22,
  input  _23,
  input  _24,
  input  _25,
  input  _26,
  output E,
  output D,
  output C,
  output B,
  output A
);

  or or_1 (E, _2, _4, _6, _8, _10, _12, _14, _16, _18, _20, _22, _24, _26);
  or or_2 (D, _3, _4, _7, _8, _11, _12, _15, _16, _19, _20, _23, _24);
  or or_3 (C, _5, _6, _7, _8, _13, _14, _15, _16, _21, _22, _23, _24);
  or or_4 (B, _9, _10, _11, _12, _13, _14, _15, _16, _25, _26);
  or or_5 (A, _17, _18, _19, _20, _21, _22, _23, _24, _25, _26);

  // Notes on the sheet:
  //   1
  //   2
  //   1
  //   2
  //   3
  //   4
  //   3
  //   4
  //   6
  //   5
  //   6
  //   5
  //   7
  //   8
  //   7
  //   8
  //   9
  //   10
  //   9
  //   10
  //   12
  //   11
  //   12
  //   11
  //   14
  //   13
  //   14
  //   13
  //   16
  //   15
  //   15
  //   16
  //   17
  //   18
  //   17
  //   18
  //   19
  //   20
  //   20
  //   19
  //   22
  //   21
  //   22
  //   21
  //   24
  //   23
  //   24
  //   23
  //   26
  //   25
  //   26
  //   25
endmodule
